// Logisim project Projet_Calculateur.circ as structural Verilog: 11 circuits, main circuit main
module main (
  input  Reset,
  input  ResetRAM
);

  wire and_1_out, Call, Clk, clock_1_out, Cond, CTRL, Exec, Fetch, getcst_1_imm, Load, ramctrl_1_memload,
       ramctrl_1_memstore, Ret, STOP, Store, WriteReg;
  wire [2:0] GetOp;
  wire [15:0] Addr, alu_1_output, Arg1, Arg2, getcst_1_cst, JMP_Address, MemIN, PC, R0, R1, R2, R3, R4, R5,
       R6, R7;
  wire [31:0] bit_extender_1_out, IR, MemOUT;

  Clock clock_1 (.out(clock_1_out));
  Seq seq_1 (.ClockOrig(and_1_out), .reset(Reset), .Clock(Clk), .Fetch(Fetch), .Exec(Exec));
  and and_1 (and_1_out, clock_1_out, ~STOP);  // AND_Gate
  LED led_1 (.in(and_1_out));
  RegPC regpc_1 (
    .Reset(Reset), .Call(Call), .Ret(Ret), .Exec(Exec), .Cond(Cond), .CTRL(CTRL), .JMP_Address(JMP_Address),
    .OutputPC(PC));
  // Probe on PC
  GetAddr getaddr_1 (.Load(Load), .Store(Store), .Fetch(Fetch), .PC(PC), .MEM_Address(Arg1), .Addr(Addr));
  // Probe on Addr
  // Probe on MemIN
  RamCtrl ramctrl_1 (
    .Load(Load), .Store(Store), .Exec(Exec), .Fetch(Fetch), .MemLoad(ramctrl_1_memload),
    .MemStore(ramctrl_1_memstore));
  LED led_2 (.in(Fetch));
  LED led_3 (.in(Exec));
  Comp comp_1 (.Arg1(Arg1), .Arg2(Arg2), .GetOp(GetOp), .Cond(Cond));
  assign bit_extender_1_out = {{16{MemIN[15]}}, MemIN};  // Bit_Extender bit_extender_1
  // Probe on PC
  // Probe on IR
  RAM #(.addrWidth(16), .clearpin("true"), .dataWidth(32), .readbehav("war")) ram_1 (
    .addr(Addr), .we(ramctrl_1_memstore), .oe(ramctrl_1_memload), .clk(Clk), .din(bit_extender_1_out),
    .dout(MemOUT), .clr(ResetRAM));
  // Probe on R0
  // Probe on R3
  // Probe on R6
  DecodeIR decodeir_1 (
    .IR(IR), .JMPAddress(JMP_Address), .STOP(STOP), .GetOp(GetOp), .CTRL(CTRL), .Call(Call), .Ret(Ret),
    .Load(Load), .Store(Store), .WriteReg(WriteReg));
  // Probe on GetOp
  // Probe on R1
  // Probe on R4
  // Probe on R7
  // Probe on R2
  // Probe on R5
  // Probe on JMP_Address
  // Probe on MemOUT
  Register #(.trigger("falling"), .width(32)) RegIR (.D(MemOUT), .clk(Fetch), .Q(IR), .clr(Reset));  // open: en
  // Probe on IR
  // Probe on R0
  Registres registres_1 (
    .Load(Load), .SR1(IR[11:9]), .Reset(Reset), .IN(alu_1_output), .SR2(IR[14:12]), .Clock(Exec),
    .MemOUT(MemOUT), .WriteReg(WriteReg), .DR(IR[8:6]), .out_20(R7), .out_10(R0), .out_11(R1), .out_13(R2),
    .out_15(R3), .out_17(R4), .out_18(R5), .out_19(R6), .OUT_DR(MemIN), .OUT_SR1(Arg1), .OUT_SR2(Arg2));
  // Probe on IR[8:6]
  // Probe on IR[11:9]
  // Probe on IR[14:12]
  ALU alu_1 (.Input1(Arg1), .Input2(Arg2), .Cst(getcst_1_cst), .Imm(getcst_1_imm), .e2(GetOp), .Output(alu_1_output));
  // Probe on getcst_1_cst
  GetCst getcst_1 (.IR(IR), .Cst(getcst_1_cst), .Imm(getcst_1_imm));
  // Probe on Arg1
  // Probe on Arg2
  // Probe on alu_1_output
  // Probe on R0
  // Probe on R1
  // Probe on R2
  // Probe on R3
  // Probe on R4
  // Probe on R5
  // Probe on R6
  // Probe on R7
  // Probe on alu_1_output

  // Notes on the sheet:
  //   Pour le fichier test :
endmodule

module ALU (
  input  [15:0] Input1,
  input  [2:0] e2,
  input  [15:0] Input2,
  input  [15:0] Cst,
  input  Imm,
  output [15:0] Output
);

  wire [3:0] bitselector_1_out;
  wire [15:0] adder_1_out, and_1_out, multiplexer_1_out, multiplier_1_out, or_1_out, shifter_1_out,
       shifter_2_out, subtractor_1_out, xor_1_out;

  Multiplexer #(.width(16)) multiplexer_1 (.in0(Input2), .in1(Cst), .out(multiplexer_1_out), .sel(Imm));
  Adder #(.width(16)) adder_1 (.a(Input1), .b(multiplexer_1_out), .out(adder_1_out));  // open: cin, cout
  Subtractor #(.width(16)) subtractor_1 (.a(Input1), .b(multiplexer_1_out), .out(subtractor_1_out));  // open: bin, bout
  Multiplier #(.width(16)) multiplier_1 (.a(Input1), .b(multiplexer_1_out), .out(multiplier_1_out));  // open: cin, cout
  assign and_1_out = Input1 & multiplexer_1_out;  // AND_Gate and_1, 16 bits wide
  assign or_1_out = Input1 | multiplexer_1_out;  // OR_Gate or_1, 16 bits wide
  assign xor_1_out = Input1 ^ multiplexer_1_out;  // XOR_Gate xor_1, 16 bits wide
  BitSelector #(.group(4), .width(16)) bitselector_1 (.in(multiplexer_1_out), .out(bitselector_1_out), .sel(2'b00));
  Shifter #(.width(16)) shifter_1 (.in(Input1), .\dist (bitselector_1_out), .out(shifter_1_out));
  Shifter #(.shift("lr"), .width(16)) shifter_2 (.in(Input1), .\dist (bitselector_1_out), .out(shifter_2_out));
  Multiplexer #(.select(3), .width(16)) multiplexer_2 (
    .in0(adder_1_out), .in1(subtractor_1_out), .in2(multiplier_1_out), .in3(and_1_out), .in4(or_1_out),
    .in5(xor_1_out), .in6(shifter_1_out), .in7(shifter_2_out), .out(Output), .sel(e2));
endmodule

module DecodeIR (
  input  [31:0] IR,
  output WriteReg,
  output CTRL,
  output Load,
  output Store,
  output [2:0] GetOp,
  output [15:0] JMPAddress,
  output STOP,
  output Call,
  output Ret
);

  wire bitselector_1_out, demultiplexer_1_out0, demultiplexer_1_out1;

  Comparator #(.width(32)) comparator_1 (.a(IR), .b({32{1'b1}}), .eq(STOP));  // open: gt, lt
  Demultiplexer #(.select(2)) demultiplexer_1 (
    .out0(demultiplexer_1_out0), .out1(demultiplexer_1_out1), .out3(CTRL), .in(1'b1), .sel(IR[1:0]));  // open: out2
  BitSelector #(.width(3)) bitselector_1 (.in(IR[4:2]), .out(bitselector_1_out), .sel(2'b00));
  Demultiplexer #(.select(3)) demultiplexer_2 (
    .out5(Call), .out6(Ret), .in(CTRL), .sel(IR[4:2]));  // open: out0, out1, out2, out3, out4, out7
  Decoder decoder_1 (.out0(Store), .out1(Load), .sel(bitselector_1_out), .en(demultiplexer_1_out1));
  or or_1 (WriteReg, demultiplexer_1_out0, Load);

  assign GetOp = IR[4:2];
  assign JMPAddress = IR[31:16];
endmodule

module GetAddr (
  input  [15:0] PC,
  input  [15:0] MEM_Address,
  input  Load,
  input  Store,
  input  Fetch,
  output [15:0] Addr
);

  wire and_1_out, or_1_out;

  or or_1 (or_1_out, Load, Store);
  and and_1 (and_1_out, or_1_out, ~Fetch);  // AND_Gate
  Multiplexer #(.width(16)) multiplexer_1 (.in0(PC), .in1(MEM_Address), .out(Addr), .sel(and_1_out));
endmodule

module GetCst (
  input  [31:0] IR,
  output [15:0] Cst,
  output Imm
);


  assign Cst = IR[31:16];
  assign Imm = IR[5];
endmodule

module RamCtrl (
  input  Exec,
  input  Fetch,
  input  Load,
  input  Store,
  output MemLoad,
  output MemStore
);

  wire and_1_out;

  and and_1 (and_1_out, Exec, Load);
  and and_2 (MemStore, Exec, Store);
  or or_1 (MemLoad, Fetch, and_1_out);
endmodule

module Registres (
  input  [2:0] SR2,
  input  Clock,
  input  Reset,
  input  [31:0] MemOUT,
  input  [2:0] SR1,
  input  [15:0] IN,
  input  WriteReg,
  input  [2:0] DR,
  input  Load,
  output [15:0] out_10,
  output [15:0] out_11,
  output [15:0] OUT_SR1,
  output [15:0] out_13,
  output [15:0] OUT_DR,
  output [15:0] out_15,
  output [15:0] OUT_SR2,
  output [15:0] out_17,
  output [15:0] out_18,
  output [15:0] out_19,
  output [15:0] out_20
);

  wire demultiplexer_2_out0, demultiplexer_2_out1, demultiplexer_2_out2, demultiplexer_2_out3,
       demultiplexer_2_out4, demultiplexer_2_out5, demultiplexer_2_out6, demultiplexer_2_out7;
  wire [2:0] multiplexer_2_out;
  wire [15:0] bitselector_1_out, controlled_buffer_1_out, demultiplexer_1_out0, demultiplexer_1_out1,
       demultiplexer_1_out2, demultiplexer_1_out3, demultiplexer_1_out4, demultiplexer_1_out5,
       demultiplexer_1_out6, demultiplexer_1_out7, multiplexer_1_out;

  // Probe on SR2
  BitSelector #(.group(16), .width(32)) bitselector_1 (.in(MemOUT), .out(bitselector_1_out), .sel(1'b0));
  Multiplexer #(.width(16)) multiplexer_1 (.in0(IN), .in1(bitselector_1_out), .out(multiplexer_1_out), .sel(Load));
  Multiplexer #(.width(3)) multiplexer_2 (.in0(DR), .in1(SR2), .out(multiplexer_2_out), .sel(Load));
  assign controlled_buffer_1_out = WriteReg ? multiplexer_1_out : 16'bz;  // Controlled_Buffer controlled_buffer_1
  Demultiplexer #(.select(3), .width(16)) demultiplexer_1 (
    .out0(demultiplexer_1_out0), .out1(demultiplexer_1_out1), .out2(demultiplexer_1_out2),
    .out3(demultiplexer_1_out3), .out4(demultiplexer_1_out4), .out5(demultiplexer_1_out5),
    .out6(demultiplexer_1_out6), .out7(demultiplexer_1_out7), .in(controlled_buffer_1_out),
    .sel(multiplexer_2_out));
  Demultiplexer #(.select(3)) demultiplexer_2 (
    .out0(demultiplexer_2_out0), .out1(demultiplexer_2_out1), .out2(demultiplexer_2_out2),
    .out3(demultiplexer_2_out3), .out4(demultiplexer_2_out4), .out5(demultiplexer_2_out5),
    .out6(demultiplexer_2_out6), .out7(demultiplexer_2_out7), .in(WriteReg), .sel(multiplexer_2_out));
  Register #(.trigger("falling"), .width(16)) R0 (
    .D(demultiplexer_1_out0), .en(demultiplexer_2_out0), .clk(Clock), .Q(out_10), .clr(Reset));
  Register #(.trigger("falling"), .width(16)) R1 (
    .D(demultiplexer_1_out1), .en(demultiplexer_2_out1), .clk(Clock), .Q(out_11), .clr(Reset));
  Register #(.trigger("falling"), .width(16)) R2 (
    .D(demultiplexer_1_out2), .en(demultiplexer_2_out2), .clk(Clock), .Q(out_13), .clr(Reset));
  Register #(.trigger("falling"), .width(16)) R3 (
    .D(demultiplexer_1_out3), .en(demultiplexer_2_out3), .clk(Clock), .Q(out_15), .clr(Reset));
  Register #(.trigger("falling"), .width(16)) R4 (
    .D(demultiplexer_1_out4), .en(demultiplexer_2_out4), .clk(Clock), .Q(out_17), .clr(Reset));
  Register #(.trigger("falling"), .width(16)) R5 (
    .D(demultiplexer_1_out5), .en(demultiplexer_2_out5), .clk(Clock), .Q(out_18), .clr(Reset));
  Register #(.trigger("falling"), .width(16)) R6 (
    .D(demultiplexer_1_out6), .en(demultiplexer_2_out6), .clk(Clock), .Q(out_19), .clr(Reset));
  Register #(.trigger("falling"), .width(16)) R7 (
    .D(demultiplexer_1_out7), .en(demultiplexer_2_out7), .clk(Clock), .Q(out_20), .clr(Reset));
  Multiplexer #(.select(3), .width(16)) multiplexer_3 (
    .in0(out_10), .in1(out_11), .in2(out_13), .in3(out_15), .in4(out_17), .in5(out_18), .in6(out_19),
    .in7(out_20), .out(OUT_SR1), .sel(SR1));
  Multiplexer #(.select(3), .width(16)) multiplexer_4 (
    .in0(out_10), .in1(out_11), .in2(out_13), .in3(out_15), .in4(out_17), .in5(out_18), .in6(out_19),
    .in7(out_20), .out(OUT_DR), .sel(SR2));

  assign OUT_SR2 = OUT_DR;

  // Other names for the same wires on the sheet: Clk = Clock; R0[15:0] = out_10; R1[15:0] = out_11; R2[15:0] = out_13;
  //   R3[15:0] = out_15; R4[15:0] = out_17; R5[15:0] = out_18; R6[15:0] = out_19; R7[15:0] = out_20

  // Notes on the sheet:
  //   IN: initial=0x1
  //   Clock: initial=0xffff
  //   LD/ST : adresse dans SR1 et écriture/lecture dans SR2
endmodule

module RegPC (
  input  Exec,
  input  Reset,
  input  Call,
  input  Ret,
  input  [15:0] JMP_Address,
  input  Cond,
  input  CTRL,
  output [15:0] OutputPC
);

  wire and_1_out;
  wire [15:0] adder_1_out, multiplexer_1_out, multiplexer_2_out, OutputPile;

  // Probe on OutputPC
  and and_1 (and_1_out, Cond, CTRL);
  Adder #(.width(16)) adder_1 (.a(OutputPC), .b(16'h1), .out(adder_1_out));  // open: cin, cout
  Multiplexer #(.width(16)) multiplexer_1 (
    .in0(adder_1_out), .in1(JMP_Address), .out(multiplexer_1_out), .sel(and_1_out));
  Multiplexer #(.width(16)) multiplexer_2 (
    .in0(multiplexer_1_out), .in1(OutputPile), .out(multiplexer_2_out), .sel(Ret));
  Pile pile_1 (.Addr(OutputPC), .Reset(Reset), .Call(Call), .Ret(Ret), .Clk(Exec), .JMP_Adress(OutputPile));
  Register #(.trigger("falling"), .width(16)) PC (
    .D(multiplexer_2_out), .en(1'b1), .clk(Exec), .Q(OutputPC), .clr(Reset));

  // Other names for the same wires on the sheet: Addr[15:0] = OutputPC
endmodule

module Seq (
  input  ClockOrig,
  input  reset,
  output Fetch,
  output Exec,
  output Clock
);

  Register #(.trigger("falling"), .width(1)) register_1 (
    .D(Fetch), .clk(ClockOrig), .Q(Exec), .clr(reset));  // open: en
  buf buffer_1 (Clock, ClockOrig);
  not not_1 (Fetch, Exec);
endmodule

module Comp (
  input  [15:0] Arg1,
  input  [15:0] Arg2,
  input  [2:0] GetOp,
  output Cond
);

  wire comparator_1_eq, comparator_1_gt, comparator_1_lt, not_1_out;

  not not_1 (not_1_out, comparator_1_eq);
  Comparator #(.width(16)) comparator_1 (
    .a(Arg1), .b(Arg2), .gt(comparator_1_gt), .eq(comparator_1_eq), .lt(comparator_1_lt));
  Multiplexer #(.enable("true"), .select(3)) multiplexer_1 (
    .in0(1'b1), .in1(comparator_1_gt), .in2(comparator_1_eq), .in3(not_1_out), .in4(comparator_1_lt),
    .in5(1'b1), .in6(1'b1), .out(Cond), .sel(GetOp));  // open: in7, en

  // Notes on the sheet:
  //   0 = JMP 1 =JSUP 2=JEQU 3=JNEQ 4=JINF 5=CALL 6=RET 7=STOP
endmodule

module Pile (
  input  Call,
  input  Ret,
  input  Reset,
  input  Clk,
  input  [15:0] Addr,
  output [15:0] JMP_Adress
);

  wire or_1_out;
  wire [15:0] adder_1_out, counter_1_q, multiplexer_1_out, register_1_q, subtractor_1_out;

  // Probe on Addr
  Register #(.width(16)) register_1 (.D(Addr), .clk(Clk), .Q(register_1_q));  // open: en, clr
  Counter #(.max('hffff), .width(16)) counter_1 (
    .count(or_1_out), .Q(counter_1_q), .up(Call), .clk(Clk), .clr(Reset));  // open: load, D, carry
  or or_1 (or_1_out, Call, Ret);
  Adder #(.width(16)) adder_1 (.a(register_1_q), .b(16'h1), .out(adder_1_out));  // open: cin, cout
  Subtractor #(.width(16)) subtractor_1 (.a(counter_1_q), .b(16'h1), .out(subtractor_1_out));  // open: bin, bout
  RAM #(.addrWidth(16), .asyncread("true"), .clearpin("true"), .dataWidth(16)) ram_1 (
    .addr(multiplexer_1_out), .we(Call), .oe(Ret), .clk(Clk), .din(adder_1_out), .dout(JMP_Adress),
    .clr(Reset));
  Multiplexer #(.width(16)) multiplexer_1 (
    .in0(counter_1_q), .in1(subtractor_1_out), .out(multiplexer_1_out), .sel(Ret));
endmodule
